// Logisim project add4bit_skeleton.circ as structural Verilog: 2 circuits, main circuit fullAdder
module fullAdder (
  input  inA,
  input  inB,
  input  carryIn,
  output sum,
  output carryOut
);

  wire and_1_out, and_2_out, and_3_out, and_4_out, and_5_out, and_6_out, and_7_out, anot, bnot, cnot;

  not not_1 (anot, inA);
  not not_2 (bnot, inB);
  not not_3 (cnot, carryIn);
  and and_1 (and_1_out, inA, inB);
  and and_2 (and_2_out, inA, carryIn);
  and and_3 (and_3_out, inB, carryIn);
  or or_1 (carryOut, and_1_out, and_2_out, and_3_out);
  and and_4 (and_4_out, carryIn, inB, inA);
  and and_5 (and_5_out, carryIn, bnot, anot);
  and and_6 (and_6_out, cnot, inB, anot);
  and and_7 (and_7_out, cnot, bnot, inA);
  or or_2 (sum, and_4_out, and_5_out, and_6_out, and_7_out);

  // Other names for the same wires on the sheet: a = inA; b = inB; c = carryIn; s = sum
endmodule

module TOP_add4bit (
  input  [3:0] A,
  input  [3:0] B,
  input  carryIn,
  output [3:0] sum,
  output carryOut
);

  wire c1, c2, c3;

  fullAdder fulladder_1 (.inA(A[0]), .inB(B[0]), .carryIn(carryIn), .sum(sum[0]), .carryOut(c1));
  fullAdder fulladder_2 (.inA(A[2]), .inB(B[2]), .carryIn(c2), .sum(sum[2]), .carryOut(c3));
  fullAdder fulladder_3 (.inA(A[1]), .inB(B[1]), .carryIn(c1), .sum(sum[1]), .carryOut(c2));
  fullAdder fulladder_4 (.inA(A[3]), .inB(B[3]), .carryIn(c3), .sum(sum[3]), .carryOut(carryOut));

  // Other names for the same wires on the sheet: cin = carryIn; cout = carryOut; s0 = sum[0]; s1 = sum[1];
  //   s2 = sum[2]; s3 = sum[3]
endmodule
