// Logisim project test_add4bit.circ as structural Verilog: 1 circuit, main circuit main
module main (
  input  rst_async
);

  wire and_2_out, and_3_out, clk, clk_gate, clk_out, comparator_1_eq, comparator_2_eq, rom_3_data,
       rom_5_data, top_add4bit_1_carryout;
  wire [3:0] rom_1_data, rom_2_data, rom_4_data, top_add4bit_1_sum;
  wire [8:0] counter_1_q;
  wire [10:0] counter_2_q, counter_3_q;

  Clock u_clk (.out(clk_out));
  and and_1 (clk, ~clk_gate, clk_out);  // AND_Gate
  Counter #(.width(9), .max('h1ff), .ongoal("stay")) counter_1 (
    .count(1'b1), .Q(counter_1_q), .carry(clk_gate), .clk(clk), .clr(rst_async));  // open: load, D
  ROM #(.addrWidth(9), .dataWidth(4)) rom_1 (.addr(counter_1_q), .data(rom_1_data));  // open: sel
  ROM #(.addrWidth(9), .dataWidth(4)) rom_2 (.addr(counter_1_q), .data(rom_2_data));  // open: sel
  ROM #(.addrWidth(9), .dataWidth(1)) rom_3 (.addr(counter_1_q), .data(rom_3_data));  // open: sel
  ROM #(.addrWidth(9), .dataWidth(4)) rom_4 (.addr(counter_1_q), .data(rom_4_data));  // open: sel
  ROM #(.addrWidth(9), .dataWidth(1)) rom_5 (.addr(counter_1_q), .data(rom_5_data));  // open: sel
  // Probe on counter_1_q
  // Probe on rom_1_data
  // Probe on rom_2_data
  // Probe on rom_3_data
  TOP_add4bit top_add4bit_1 (
    .A(rom_1_data), .B(rom_2_data), .carryIn(rom_3_data), .sum(top_add4bit_1_sum),
    .carryOut(top_add4bit_1_carryout));
  // Probe on top_add4bit_1_sum
  // Probe on rom_4_data
  // Probe on counter_2_q
  // Probe on counter_3_q
  Comparator #(.width(4)) comparator_1 (.a(top_add4bit_1_sum), .b(rom_4_data), .eq(comparator_1_eq));  // open: gt, lt
  Comparator #(.width(1)) comparator_2 (
    .a(top_add4bit_1_carryout), .b(rom_5_data), .eq(comparator_2_eq));  // open: gt, lt
  and and_2 (and_2_out, ~comparator_1_eq, 1'b1);  // AND_Gate
  and and_3 (and_3_out, ~comparator_2_eq, 1'b1);  // AND_Gate
  Counter #(.width(11), .max('h7ff)) counter_2 (
    .count(and_2_out), .Q(counter_2_q), .clk(clk), .clr(rst_async));  // open: load, D, carry
  Counter #(.width(11), .max('h7ff)) counter_3 (
    .count(and_3_out), .Q(counter_3_q), .clk(clk), .clr(rst_async));  // open: load, D, carry

  // Notes on the sheet:
  //   contents of rom_1 (hex, n*v repeats v):
  //   0 1 2 3 4 5 6 7 8 9 a b c d e f 0 1 2 3 4 5 6 7 8 9 a b c d e f 0 1 2 3 4 5 6 7 8 9 a b c d e f 0 1
  //   2 3 4 5 6 7 8 9 a b c d e f 0 1 2 3 4 5 6 7 8 9 a b c d e f 0 1 2 3 4 5 6 7 8 9 a b c d e f 0 1 2 3
  //   4 5 6 7 8 9 a b c d e f 0 1 2 3 4 5 6 7 8 9 a b c d e f 0 1 2 3 4 5 6 7 8 9 a b c d e f 0 1 2 3 4 5
  //   6 7 8 9 a b c d e f 0 1 2 3 4 5 6 7 8 9 a b c d e f 0 1 2 3 4 5 6 7 8 9 a b c d e f 0 1 2 3 4 5 6 7
  //   8 9 a b c d e f 0 1 2 3 4 5 6 7 8 9 a b c d e f 0 1 2 3 4 5 6 7 8 9 a b c d e f 0 1 2 3 4 5 6 7 8 9
  //   a b c d e f 0 1 2 3 4 5 6 7 8 9 a b c d e f 0 1 2 3 4 5 6 7 8 9 a b c d e f 0 1 2 3 4 5 6 7 8 9 a b
  //   c d e f 0 1 2 3 4 5 6 7 8 9 a b c d e f 0 1 2 3 4 5 6 7 8 9 a b c d e f 0 1 2 3 4 5 6 7 8 9 a b c d
  //   e f 0 1 2 3 4 5 6 7 8 9 a b c d e f 0 1 2 3 4 5 6 7 8 9 a b c d e f 0 1 2 3 4 5 6 7 8 9 a b c d e f
  //   0 1 2 3 4 5 6 7 8 9 a b c d e f 0 1 2 3 4 5 6 7 8 9 a b c d e f 0 1 2 3 4 5 6 7 8 9 a b c d e f 0 1
  //   2 3 4 5 6 7 8 9 a b c d e f 0 1 2 3 4 5 6 7 8 9 a b c d e f 0 1 2 3 4 5 6 7 8 9 a b c d e f 0 1 2 3
  //   4 5 6 7 8 9 a b c d e f
  //   A
  //   contents of rom_2 (hex, n*v repeats v):
  //   16*0 16*1 16*2 16*3 16*4 16*5 16*6 16*7 16*8 16*9 16*a 16*b 16*c 16*d 16*e 16*f 16*0 16*1 16*2 16*3
  //   16*4 16*5 16*6 16*7 16*8 16*9 16*a 16*b 16*c 16*d 16*e 16*f
  //   B
  //   contents of rom_3 (hex, n*v repeats v):
  //   256*0 256*1
  //   carryIn
  //   contents of rom_4 (hex, n*v repeats v):
  //   0 1 2 3 4 5 6 7 8 9 a b c d e f 1 2 3 4 5 6 7 8 9 a b c d e f 0 2 3 4 5 6 7 8 9 a b c d e f 0 1 3 4
  //   5 6 7 8 9 a b c d e f 0 1 2 4 5 6 7 8 9 a b c d e f 0 1 2 3 5 6 7 8 9 a b c d e f 0 1 2 3 4 6 7 8 9
  //   a b c d e f 0 1 2 3 4 5 7 8 9 a b c d e f 0 1 2 3 4 5 6 8 9 a b c d e f 0 1 2 3 4 5 6 7 9 a b c d e
  //   f 0 1 2 3 4 5 6 7 8 a b c d e f 0 1 2 3 4 5 6 7 8 9 b c d e f 0 1 2 3 4 5 6 7 8 9 a c d e f 0 1 2 3
  //   4 5 6 7 8 9 a b d e f 0 1 2 3 4 5 6 7 8 9 a b c e f 0 1 2 3 4 5 6 7 8 9 a b c d f 0 1 2 3 4 5 6 7 8
  //   9 a b c d e 1 2 3 4 5 6 7 8 9 a b c d e f 0 2 3 4 5 6 7 8 9 a b c d e f 0 1 3 4 5 6 7 8 9 a b c d e
  //   f 0 1 2 4 5 6 7 8 9 a b c d e f 0 1 2 3 5 6 7 8 9 a b c d e f 0 1 2 3 4 6 7 8 9 a b c d e f 0 1 2 3
  //   4 5 7 8 9 a b c d e f 0 1 2 3 4 5 6 8 9 a b c d e f 0 1 2 3 4 5 6 7 9 a b c d e f 0 1 2 3 4 5 6 7 8
  //   a b c d e f 0 1 2 3 4 5 6 7 8 9 b c d e f 0 1 2 3 4 5 6 7 8 9 a c d e f 0 1 2 3 4 5 6 7 8 9 a b d e
  //   f 0 1 2 3 4 5 6 7 8 9 a b c e f 0 1 2 3 4 5 6 7 8 9 a b c d f 0 1 2 3 4 5 6 7 8 9 a b c d e 0 1 2 3
  //   4 5 6 7 8 9 a b c d e f
  //   expect_sum
  //   contents of rom_5 (hex, n*v repeats v):
  //   31*0 1 14*0 1 1 13*0 1 1 1 12*0 4*1 11*0 5*1 10*0 6*1 9*0 7*1 8*0 8*1 7*0 9*1 6*0 10*1 5*0 11*1 4*0
  //   12*1 0 0 0 13*1 0 0 14*1 0 15*1 15*0 1 14*0 1 1 13*0 1 1 1 12*0 4*1 11*0 5*1 10*0 6*1 9*0 7*1 8*0
  //   8*1 7*0 9*1 6*0 10*1 5*0 11*1 4*0 12*1 0 0 0 13*1 0 0 14*1 0 31*1
  //   expect_cout
  //   sum
endmodule
